// Logisim project 3-bit parity generator & checker.circ as structural Verilog: 1 circuit, main circuit main
// (Even sum)
module main (
  input  A,
  input  B,
  input  A_2,
  input  C,
  input  B_2,
  input  P,
  input  C_2,
  input  A_3,
  input  B_3,
  input  A_4,
  input  C_3,
  input  B_4,
  input  P_2,
  input  C_4,
  output A_5,
  output B_5,
  output C_5,
  output P_3,
  output A_6,
  output B_6,
  output C_6,
  output P_4
);

  wire not_1_out, not_2_out, xnor_2_out, xnor_3_out, xnor_4_out, xor_1_out, xor_2_out, xor_5_out, xor_6_out,
       xor_7_out;

  xor xor_1 (xor_1_out, A_2, B_2);
  xor xor_2 (xor_2_out, A_4, B_4);
  xor xor_3 (P_3, xor_1_out, C_2);
  xnor xnor_1 (P_4, xor_2_out, C_4);
  // XOR_Gate xor_4 has open pins: in0=xor_2_out, in1=C_4, out=open
  xor xor_5 (xor_5_out, A, B);
  xor xor_6 (xor_6_out, C, P);
  xnor xnor_2 (xnor_2_out, A_3, B_3);
  xnor xnor_3 (xnor_3_out, C_3, P_2);
  not not_1 (not_1_out, xor_7_out);
  xor xor_7 (xor_7_out, xor_5_out, xor_6_out);
  xnor xnor_4 (xnor_4_out, xnor_2_out, xnor_3_out);
  not not_2 (not_2_out, xnor_4_out);
  LED led_1 (.in(not_1_out));
  LED led_2 (.in(xor_7_out));
  LED led_3 (.in(not_2_out));
  LED led_4 (.in(xnor_4_out));

  assign A_5 = A_2;
  assign A_6 = A_4;
  assign B_5 = B_2;
  assign B_6 = B_4;
  assign C_5 = C_2;
  assign C_6 = C_4;

  // Notes on the sheet:
  //   3-bit even parity generator circuit
  //   3-bit odd parity generator circuit
  //   Transmitter
  //   3-bit parity generators & checkers
  //   3-bit Even Parity checker circuit
  //   3-bit Odd Parity Checker circuit
  //   Receiver 
  //   Error-free
  //   Error !!
  //   Error-free
  //   Error !!
  //   (Even sum)
  //   (Even sum)
  //   (Even sum)
  //   (Even sum)
  //   (Even sum)
  //   (Odd sum)
  //   (Odd sum)
  //   (Even sum)
endmodule
